# Fritzing sketch lightswitcher_diagramm (saved by Fritzing 0.9.3b)
breadboards: 1

parts:
  U1 = ATTINY45 [package=dip]
  S1 = Pushbutton [package="[THT]"]
  R1 = Resistor [tolerance=±5% resistance=220 package=THT]
  U7 = RF-LINK_TX [package=rf-link_tx]

nets:
  N1: U1.PB4(ADC2), S1.Pin_1, S1.Pin_2, R1.Pin_1
  N2: U1.PB0(MOSI), U7.DATA
  VCC: U1.VCC, S1.Pin_3, S1.Pin_4, U7.+5V
  N3: R1.Pin_0, U7.GND

custom parts:
  RF-LINK_TX: Common RF transmitter of the 315.00Mhz varity
